// Logisim project 13129589.circ as structural Verilog: 1 circuit, main circuit main
module main (
  input  W,
  input  X,
  input  Y,
  input  Z,
  output G,
  output F,
  output E,
  output D,
  output C,
  output B,
  output A
);

  wire and_1_out, and_2_out, and_3_out, and_4_out, and_5_out, and_6_out, and_7_out, and_8_out, and_9_out,
       and_10_out, and_11_out, and_12_out, not_1_out, not_2_out, not_3_out, not_4_out, not_5_out, not_6_out,
       not_7_out, not_8_out, not_9_out, not_10_out, not_11_out, not_12_out;

  not not_1 (not_1_out, Y);
  and and_1 (and_1_out, not_1_out, X);
  not not_2 (not_2_out, X);
  not not_3 (not_3_out, W);
  not not_4 (not_4_out, X);
  not not_5 (not_5_out, W);
  not not_6 (not_6_out, Y);
  not not_7 (not_7_out, X);
  not not_8 (not_8_out, X);
  not not_9 (not_9_out, X);
  not not_10 (not_10_out, W);
  not not_11 (not_11_out, Y);
  and and_2 (and_2_out, Y, not_2_out);
  not not_12 (not_12_out, W);
  and and_3 (and_3_out, not_3_out, Y);
  and and_4 (and_4_out, not_4_out, Y);
  and and_5 (and_5_out, X, not_5_out);
  and and_6 (and_6_out, W, Y, not_7_out);
  and and_7 (and_7_out, W, X);
  and and_8 (and_8_out, not_9_out, not_10_out);
  and and_9 (and_9_out, Y, W);
  and and_10 (and_10_out, not_10_out, not_11_out);
  and and_11 (and_11_out, Y, not_12_out);
  and and_12 (and_12_out, X, not_6_out);
  or or_1 (G, Z, and_1_out, and_2_out, and_11_out);
  or or_2 (F, Z, and_3_out, and_4_out, and_8_out);
  or or_3 (E, and_5_out, and_10_out);
  or or_4 (D, and_5_out, and_12_out, Z, and_6_out, and_10_out);
  or or_5 (C, Y, not_8_out, W);
  or or_6 (B, and_7_out, and_8_out, not_11_out);
  or or_7 (A, X, and_9_out, Z, and_10_out);
  _7_Segment_Display u_7_segment_display_1 (.g(G), .f(F), .a(A), .b(B), .e(E), .d(D), .c(C));  // open: dp
endmodule
